// Logisim project PipelinedProcesserArch.circ as structural Verilog: 15 circuits, main circuit RegFile
module PiplinedProcessor (
);

  wire ALUSrc, and_1_out, and_2_out, and_3_out, clk_out, ex_mem_1_p10, ex_mem_1_p11, ex_mem_1_p12, ExecuteEn,
       id_ex_1_alusrc_ex, id_ex_1_memwrite_ex, id_ex_1_regwrite_ex, KillSignal, killSignal_t,
       mem_wb_1_regwrite_wb, MemRead, MemRead_EX, MemRead_IDEX, MemWrite, MemWrite_IDEX, not_1_out,
       not_2_out, not_3_out, RegDst, RegReadSrc2, RegWrite, RegWrite_IDEX, StallSignal;
  wire [1:0] ExtSel, fwd_rp, fwd_rs, fwd_rt, id_ex_1_wb_sel_ex, mem_wb_1_wb_sel_wb, PCSel, WB_Sel, WB_Sel_MEM;
  wire [2:0] ALUOp, id_ex_1_alu_op_ex;
  wire [4:0] Opcode, Rd, Rd_Addr_EX, Rd_Addr_MEM, Rd_Addr_WB, Real_Rd_Addr, Real_Rt_Addr, Rp, Rs, Rt;
  wire [11:0] decodestage_splitter_1_immediate;
  wire [21:0] decodestage_splitter_1_offset;
  wire [31:0] adder_1_out, ALU_Result_EX, ALU_Result_MEM, current_pc, ex_mem_1_p15, ExtOut, Final_Data_WB,
       id_ex_1_extimm_ex, id_ex_1_pc_plus_1_ex, id_ex_1_rtdata_ex, if_id_1_instruction_d, if_id_1_pc_d,
       mem_wb_1_alu_result_wb, mem_wb_1_memdata_wb, mem_wb_1_pc_plus_1_wb, MemData_MEM, multiplexer_2_out,
       multiplexer_8_out, multiplexer_9_out, multiplexer_10_out, multiplexer_11_out, multiplexer_12_out,
       next_pc_to_RF, pc_control_1_next_pc, PC_plus_1_MEM, regfile_1_rpdata, regfile_1_rsdata,
       regfile_1_rtdata, rom_1_data, undriven;

  Clock clk (.out(clk_out));
  PC_Control pc_control_1 (
    .current_pc(current_pc), .sign_ext_off(ExtOut), .ExecuteEn(ExecuteEn), .PCSrc(PCSel),
    .next_pc(pc_control_1_next_pc));  // open: rs_data
  Multiplexer #(.width(32), .enable("false")) multiplexer_1 (
    .in0(pc_control_1_next_pc), .in1(current_pc), .out(next_pc_to_RF), .sel(StallSignal));
  ROM #(.addrWidth(10), .dataWidth(32)) rom_1 (.addr(current_pc[9:0]), .data(rom_1_data));  // open: sel
  Multiplexer #(.width(32), .enable("false")) multiplexer_2 (
    .in0(rom_1_data), .in1({32{1'b0}}), .out(multiplexer_2_out), .sel(killSignal_t));
  Adder #(.width(32)) adder_1 (.a(current_pc), .b(32'h1), .out(adder_1_out));  // open: cin, cout
  IF_ID if_id_1 (
    .PC_F(adder_1_out), .stall(StallSignal), .clk(clk_out), .kill(killSignal_t),
    .Instruction_D(if_id_1_instruction_d), .PC_D(if_id_1_pc_d));  // open: Instruction_F
  ControlUnit controlunit_1 (
    .RegWrite(RegWrite), .ALUSrc(ALUSrc), .Opcode(Opcode), .RegDst(RegDst), .ALUOp(ALUOp), .MemRead(MemRead),
    .WB_Sel(WB_Sel), .PCSel(PCSel), .MemWrite(MemWrite), .RegReadSrc2(RegReadSrc2), .ExtSel(ExtSel));
  DecodeStage_splitter decodestage_splitter_1 (
    .Immediate(decodestage_splitter_1_immediate), .Offset(decodestage_splitter_1_offset),
    .Inst(if_id_1_instruction_d));  // open: OPCode, Rp, Rd, Rs, Rt
  Extender extender_1 (
    .Imm12(decodestage_splitter_1_immediate), .Offset22(decodestage_splitter_1_offset), .ExtSel(ExtSel),
    .ExOut(ExtOut));
  ForwardingUnit forwardingunit_1 (
    .SrcAddr(Rs), .Rd_Ex(Rd_Addr_EX), .RegWrite_EX(id_ex_1_regwrite_ex), .Rd_MEM(Rd_Addr_MEM),
    .RegWrite_MEM(ex_mem_1_p10), .Rd_WB(Rd_Addr_WB), .RegWrite_WB(mem_wb_1_regwrite_wb), .Forward(fwd_rs));
  not not_1 (not_1_out, StallSignal);
  not not_2 (not_2_out, StallSignal);
  not not_3 (not_3_out, StallSignal);
  Multiplexer #(.width(5), .enable("false")) multiplexer_3 (.in0(Rt), .in1(Rd), .out(Real_Rt_Addr), .sel(RegReadSrc2));
  Multiplexer #(.width(5), .enable("false")) multiplexer_4 (
    .in0(Rd), .in1({5{1'b1}}), .out(Real_Rd_Addr), .sel(RegDst));
  Multiplexer #(.enable("false")) multiplexer_5 (.in0(1'b0), .in1(MemRead), .out(MemRead_IDEX), .sel(and_1_out));
  and and_1 (and_1_out, ExecuteEn, not_1_out);
  Multiplexer #(.enable("false")) multiplexer_6 (.in0(1'b0), .in1(MemWrite), .out(MemWrite_IDEX), .sel(and_2_out));
  and and_2 (and_2_out, ExecuteEn, not_2_out);
  Multiplexer #(.enable("false")) multiplexer_7 (.in0(1'b0), .in1(RegWrite), .out(RegWrite_IDEX), .sel(and_3_out));
  and and_3 (and_3_out, ExecuteEn, not_3_out);
  RegFile regfile_1 (
    .Rs(Rs), .Rt(Real_Rt_Addr), .RegDest(Real_Rd_Addr), .RegWrite(mem_wb_1_regwrite_wb),
    .RsData(regfile_1_rsdata), .RtData(regfile_1_rtdata), .CLK(clk_out), .RpData(regfile_1_rpdata),
    .next_pc(if_id_1_pc_d), .current_pc(current_pc));  // open: data_in, Rp
  ForwardingUnit forwardingunit_2 (
    .SrcAddr(Rp), .Rd_Ex(Rd_Addr_EX), .RegWrite_EX(id_ex_1_regwrite_ex), .Rd_MEM(Rd_Addr_MEM),
    .RegWrite_MEM(ex_mem_1_p10), .Rd_WB(Rd_Addr_WB), .RegWrite_WB(mem_wb_1_regwrite_wb), .Forward(fwd_rp));
  StallUnit stallunit_1 (
    .forrward_rs(fwd_rs), .MemRead_EX(MemRead_EX), .forward_rt(fwd_rp), .forward_rp(fwd_rt),
    .Stall(StallSignal));
  Multiplexer #(.select(2), .width(32), .enable("false")) multiplexer_8 (
    .in0(ALU_Result_MEM), .in1(MemData_MEM), .in2(PC_plus_1_MEM), .in3(ALU_Result_MEM),
    .out(multiplexer_8_out), .sel(WB_Sel_MEM));
  ForwardingUnit forwardingunit_3 (
    .SrcAddr(Real_Rt_Addr), .Rd_Ex(Rd_Addr_EX), .RegWrite_EX(id_ex_1_regwrite_ex), .Rd_MEM(Rd_Addr_MEM),
    .RegWrite_MEM(ex_mem_1_p10), .Rd_WB(Rd_Addr_WB), .RegWrite_WB(mem_wb_1_regwrite_wb), .Forward(fwd_rt));
  Multiplexer #(.select(2), .width(32), .enable("false")) multiplexer_9 (
    .in0(regfile_1_rsdata), .in1(ALU_Result_EX), .in2(multiplexer_8_out), .in3(Final_Data_WB),
    .out(multiplexer_9_out), .sel(fwd_rs));
  Multiplexer #(.select(2), .width(32), .enable("false")) multiplexer_10 (
    .in0(regfile_1_rtdata), .in1(ALU_Result_EX), .in2(multiplexer_8_out), .in3(Final_Data_WB),
    .out(multiplexer_10_out), .sel(fwd_rt));
  Multiplexer #(.select(2), .width(32), .enable("false")) multiplexer_11 (
    .in0(regfile_1_rpdata), .in1(ALU_Result_EX), .in2(multiplexer_8_out), .in3(Final_Data_WB),
    .out(multiplexer_11_out), .sel(fwd_rp));
  PredicateUnit predicateunit_1 (.Rp_addr(Rp), .Rp_data(multiplexer_11_out), .ExecuteEn(ExecuteEn));
  KillUnit killunit_1 (.Opcode(Opcode), .Kill(KillSignal), .ExecuteEn(ExecuteEn));
  ID_EX id_ex_1 (
    .RegWrite_D(RegWrite_IDEX), .MemRead_D(MemRead_IDEX), .MemWrite_D(MemWrite_IDEX), .ALUSrc_D(ALUSrc),
    .WB_Sel_D(WB_Sel), .ALU_OP_D(ALUOp), .RsData_D(multiplexer_9_out), .RtData_D(multiplexer_10_out),
    .PC_plus_1_D(if_id_1_pc_d), .Rd_Addr_D(Real_Rd_Addr), .Rs_Addr_D(Rs), .Rt_Addr_D(Real_Rt_Addr),
    .CLK(clk_out), .RegWrite_EX(id_ex_1_regwrite_ex), .MemRead_EX(MemRead_EX),
    .MemWrite_EX(id_ex_1_memwrite_ex), .ALUSrc_EX(id_ex_1_alusrc_ex), .WB_Sel_EX(id_ex_1_wb_sel_ex),
    .ALU_OP_EX(id_ex_1_alu_op_ex), .RtData_EX(id_ex_1_rtdata_ex), .PC_plus_1_EX(id_ex_1_pc_plus_1_ex),
    .Rd_Addr_EX(Rd_Addr_EX), .stall(StallSignal), .kill(1'b0), .ExtImm_D(ExtOut),
    .ExtImm_EX(id_ex_1_extimm_ex));  // open: RsData_EX, Rs_Addr_EX, Rt_Addr_EX
  Multiplexer #(.width(32), .enable("false")) multiplexer_12 (
    .in0(id_ex_1_rtdata_ex), .in1(id_ex_1_extimm_ex), .out(multiplexer_12_out), .sel(id_ex_1_alusrc_ex));
  ALU alu_1 (.IN1(undriven), .ALUres(ALU_Result_EX), .AluSel(id_ex_1_alu_op_ex));  // open: IN2
  // EX_MEM ex_mem_1: pin names not known; wires that end beside it: id_ex_1_regwrite_ex, MemRead_EX, id_ex_1_memwrite_ex, ALU_Result_EX, Rd_Addr_EX, id_ex_1_wb_sel_ex, id_ex_1_rtdata_ex, id_ex_1_pc_plus_1_ex, clk_out, ex_mem_1_p10, ex_mem_1_p11, ex_mem_1_p12, WB_Sel_MEM, ALU_Result_MEM, ex_mem_1_p15, PC_plus_1_MEM, Rd_Addr_MEM
  RAM #(.addrWidth(10), .dataWidth(32), .bus("separate")) ram_1 (
    .addr(ALU_Result_MEM[9:0]), .din(ex_mem_1_p15), .data(MemData_MEM), .str(ex_mem_1_p12), .clk(clk_out),
    .ld(ex_mem_1_p11));  // open: sel, clr
  MEM_WB mem_wb_1 (
    .RegWrite_MEM(ex_mem_1_p10), .WB_Sel_MEM(WB_Sel_MEM), .ALU_Result_MEM(ALU_Result_MEM),
    .MemData_MEM(MemData_MEM), .PC_plus_1_MEM(PC_plus_1_MEM), .Rd_Addr_MEM(Rd_Addr_MEM), .clk(clk_out),
    .RegWrite_WB(mem_wb_1_regwrite_wb), .WB_Sel_WB(mem_wb_1_wb_sel_wb),
    .ALU_Result_WB(mem_wb_1_alu_result_wb), .MemData_WB(mem_wb_1_memdata_wb),
    .PC_plus_1_WB(mem_wb_1_pc_plus_1_wb), .Rd_Addr_WB(Rd_Addr_WB));
  Multiplexer #(.select(2), .width(32), .enable("false")) multiplexer_13 (
    .in0(mem_wb_1_alu_result_wb), .in1(mem_wb_1_memdata_wb), .in2(mem_wb_1_pc_plus_1_wb),
    .in3(mem_wb_1_alu_result_wb), .out(Final_Data_WB), .sel(mem_wb_1_wb_sel_wb));
endmodule

// REG
module RegFile (
  input  [4:0] Rt,
  input  [4:0] Rp,
  input  [4:0] Rs,
  input  [31:0] data_in,
  input  RegWrite,
  input  CLK,
  input  [4:0] RegDest,
  input  [31:0] next_pc,
  output [31:0] current_pc,
  output [31:0] RpData,
  output [31:0] RtData,
  output [31:0] RsData
);

  wire and_1_out, and_2_out, and_3_out, and_4_out, and_5_out, and_6_out, and_7_out, and_8_out, and_9_out,
       and_10_out, and_11_out, and_12_out, and_13_out, and_14_out, and_15_out, and_16_out, and_17_out,
       and_18_out, and_19_out, and_20_out, and_21_out, and_22_out, and_23_out, and_24_out, and_25_out,
       and_26_out, and_27_out, and_28_out, and_29_out, and_30_out, and_31_out, decoder_1_out0,
       decoder_2_out0, decoder_2_out1, decoder_2_out2, decoder_2_out3, decoder_2_out4, decoder_2_out5,
       decoder_2_out6, decoder_2_out7, decoder_2_out8, decoder_2_out9, decoder_2_out10, decoder_2_out11,
       decoder_2_out12, decoder_2_out13, decoder_2_out14, decoder_2_out15, decoder_2_out16, decoder_2_out17,
       decoder_2_out18, decoder_2_out19, decoder_2_out20, decoder_2_out21, decoder_2_out22, decoder_2_out23,
       decoder_2_out24, decoder_2_out25, decoder_2_out26, decoder_2_out27, decoder_2_out28, decoder_2_out29,
       decoder_2_out30, decoder_2_out31, decoder_3_out0, decoder_3_out1, decoder_3_out2, decoder_3_out3,
       decoder_3_out4, decoder_3_out5, decoder_3_out6, decoder_3_out7, decoder_3_out8, decoder_3_out9,
       decoder_3_out10, decoder_3_out11, decoder_3_out12, decoder_3_out13, decoder_3_out14, decoder_3_out15,
       decoder_3_out16, decoder_3_out17, decoder_3_out18, decoder_3_out19, decoder_3_out20, decoder_3_out21,
       decoder_3_out22, decoder_3_out23, decoder_3_out24, decoder_3_out25, decoder_3_out26, decoder_3_out27,
       decoder_3_out28, decoder_3_out29, decoder_3_out30, decoder_3_out31, decoder_4_out0, decoder_4_out1,
       decoder_4_out2, decoder_4_out3, decoder_4_out4, decoder_4_out5, decoder_4_out6, decoder_4_out7,
       decoder_4_out8, decoder_4_out9, decoder_4_out10, decoder_4_out11, decoder_4_out12, decoder_4_out13,
       decoder_4_out14, decoder_4_out15, decoder_4_out16, decoder_4_out17, decoder_4_out18, decoder_4_out19,
       decoder_4_out20, decoder_4_out21, decoder_4_out22, decoder_4_out23, decoder_4_out24, decoder_4_out25,
       decoder_4_out26, decoder_4_out27, decoder_4_out28, decoder_4_out29, decoder_4_out30, decoder_4_out31,
       r1, r2, r3, r4, r5, r6, r7, r8, r9, r10, r11, r12, r13, r14, r15, r16, r17, r18, r19, r20, r21, r22,
       r23, r24, r25, r26, r27, r28, r29, r30, r31;
  wire [31:0] R1_q, R2_q, R3_q, R4_q, R5_q, R6_q, R7_q, R8_q, R9_q, R10_q, R11_q, R12_q, R13_q, R14_q, R15_q,
       R16_q, R17_q, R18_q, R19_q, R20_q, R21_q, R22_q, R23_q, R24_q, R25_q, R26_q, R27_q, R28_q, R29_q,
       R31_q;

  Decoder #(.select(5), .enable("false")) decoder_1 (
    .out0(decoder_1_out0), .out1(r1), .out2(r2), .out3(r3), .out4(r4), .out5(r5), .out6(r6), .out7(r7),
    .out8(r8), .out9(r9), .out10(r10), .out11(r11), .out12(r12), .out13(r13), .out14(r14), .out15(r15),
    .out16(r16), .out17(r17), .out18(r18), .out19(r19), .out20(r20), .out21(r21), .out22(r22), .out23(r23),
    .out24(r24), .out25(r25), .out26(r26), .out27(r27), .out28(r28), .out29(r29), .out30(r30), .out31(r31),
    .sel(RegDest));
  and and_1 (and_1_out, r1, RegWrite);
  and and_2 (and_2_out, r2, RegWrite);
  and and_3 (and_3_out, r3, RegWrite);
  and and_4 (and_4_out, r4, RegWrite);
  and and_5 (and_5_out, r5, RegWrite);
  and and_6 (and_6_out, r6, RegWrite);
  and and_7 (and_7_out, r7, RegWrite);
  and and_8 (and_8_out, r8, RegWrite);
  and and_9 (and_9_out, r9, RegWrite);
  and and_10 (and_10_out, r10, RegWrite);
  and and_11 (and_11_out, r11, RegWrite);
  and and_12 (and_12_out, r12, RegWrite);
  and and_13 (and_13_out, r13, RegWrite);
  and and_14 (and_14_out, r14, RegWrite);
  and and_15 (and_15_out, r15, RegWrite);
  and and_16 (and_16_out, r16, RegWrite);
  and and_17 (and_17_out, r17, RegWrite);
  and and_18 (and_18_out, r18, RegWrite);
  and and_19 (and_19_out, r19, RegWrite);
  and and_20 (and_20_out, r20, RegWrite);
  and and_21 (and_21_out, r21, RegWrite);
  and and_22 (and_22_out, r22, RegWrite);
  and and_23 (and_23_out, r23, RegWrite);
  and and_24 (and_24_out, r24, RegWrite);
  and and_25 (and_25_out, r25, RegWrite);
  and and_26 (and_26_out, r26, RegWrite);
  and and_27 (and_27_out, r27, RegWrite);
  and and_28 (and_28_out, r28, RegWrite);
  and and_29 (and_29_out, r29, RegWrite);
  and and_30 (and_30_out, r30, 1'b1);
  and and_31 (and_31_out, r31, RegWrite);
  assign RsData = decoder_2_out0 ? {32{1'b0}} : 32'bz;  // Controlled_Buffer controlled_buffer_1
  assign RsData = decoder_2_out1 ? R1_q : 32'bz;  // Controlled_Buffer controlled_buffer_2
  Register #(.width(32)) u_R1 (.D(data_in), .en(and_1_out), .Q(R1_q), .clk(CLK));  // open: clr
  assign RsData = decoder_2_out2 ? R2_q : 32'bz;  // Controlled_Buffer controlled_buffer_3
  Register #(.width(32)) u_R2 (.D(data_in), .en(and_2_out), .Q(R2_q), .clk(CLK));  // open: clr
  assign RsData = decoder_2_out3 ? R3_q : 32'bz;  // Controlled_Buffer controlled_buffer_4
  Register #(.width(32)) u_R3 (.D(data_in), .en(and_3_out), .Q(R3_q), .clk(CLK));  // open: clr
  assign RsData = decoder_2_out4 ? R4_q : 32'bz;  // Controlled_Buffer controlled_buffer_5
  Register #(.width(32)) u_R4 (.D(data_in), .en(and_4_out), .Q(R4_q), .clk(CLK));  // open: clr
  assign RsData = decoder_2_out5 ? R5_q : 32'bz;  // Controlled_Buffer controlled_buffer_6
  Register #(.width(32)) u_R5 (.D(data_in), .en(and_5_out), .Q(R5_q), .clk(CLK));  // open: clr
  assign RsData = decoder_2_out6 ? R6_q : 32'bz;  // Controlled_Buffer controlled_buffer_7
  Register #(.width(32)) u_R6 (.D(data_in), .en(and_6_out), .Q(R6_q), .clk(CLK));  // open: clr
  assign RsData = decoder_2_out7 ? R7_q : 32'bz;  // Controlled_Buffer controlled_buffer_8
  Register #(.width(32)) u_R7 (.D(data_in), .en(and_7_out), .Q(R7_q), .clk(CLK));  // open: clr
  assign RsData = decoder_2_out8 ? R8_q : 32'bz;  // Controlled_Buffer controlled_buffer_9
  Register #(.width(32)) u_R8 (.D(data_in), .en(and_8_out), .Q(R8_q), .clk(CLK));  // open: clr
  assign RsData = decoder_2_out9 ? R9_q : 32'bz;  // Controlled_Buffer controlled_buffer_10
  Register #(.width(32)) u_R9 (.D(data_in), .en(and_9_out), .Q(R9_q), .clk(CLK));  // open: clr
  Register #(.width(32)) u_R10 (.D(data_in), .en(and_10_out), .Q(R10_q), .clk(CLK));  // open: clr
  assign RsData = decoder_2_out10 ? R10_q : 32'bz;  // Controlled_Buffer controlled_buffer_11
  Register #(.width(32)) u_R11 (.D(data_in), .en(and_11_out), .Q(R11_q), .clk(CLK));  // open: clr
  assign RsData = decoder_2_out11 ? R11_q : 32'bz;  // Controlled_Buffer controlled_buffer_12
  Register #(.width(32)) u_R12 (.D(data_in), .en(and_12_out), .Q(R12_q), .clk(CLK));  // open: clr
  assign RsData = decoder_2_out12 ? R12_q : 32'bz;  // Controlled_Buffer controlled_buffer_13
  assign RsData = decoder_2_out13 ? R13_q : 32'bz;  // Controlled_Buffer controlled_buffer_14
  Register #(.width(32)) u_R13 (.D(data_in), .en(and_13_out), .Q(R13_q), .clk(CLK));  // open: clr
  assign RsData = decoder_2_out14 ? R14_q : 32'bz;  // Controlled_Buffer controlled_buffer_15
  Register #(.width(32)) u_R14 (.D(data_in), .en(and_14_out), .Q(R14_q), .clk(CLK));  // open: clr
  Register #(.width(32)) u_R15 (.D(data_in), .en(and_15_out), .Q(R15_q), .clk(CLK));  // open: clr
  assign RsData = decoder_2_out15 ? R15_q : 32'bz;  // Controlled_Buffer controlled_buffer_16
  assign RsData = decoder_2_out16 ? R16_q : 32'bz;  // Controlled_Buffer controlled_buffer_17
  Register #(.width(32)) u_R16 (.D(data_in), .en(and_16_out), .Q(R16_q), .clk(CLK));  // open: clr
  assign RsData = decoder_2_out17 ? R17_q : 32'bz;  // Controlled_Buffer controlled_buffer_18
  Register #(.width(32)) u_R17 (.D(data_in), .en(and_17_out), .Q(R17_q), .clk(CLK));  // open: clr
  Register #(.width(32)) u_R18 (.D(data_in), .en(and_18_out), .Q(R18_q), .clk(CLK));  // open: clr
  assign RsData = decoder_2_out18 ? R18_q : 32'bz;  // Controlled_Buffer controlled_buffer_19
  assign RsData = decoder_2_out19 ? R19_q : 32'bz;  // Controlled_Buffer controlled_buffer_20
  Register #(.width(32)) u_R19 (.D(data_in), .en(and_19_out), .Q(R19_q), .clk(CLK));  // open: clr
  Register #(.width(32)) u_R20 (.D(data_in), .en(and_20_out), .Q(R20_q), .clk(CLK));  // open: clr
  assign RsData = decoder_2_out20 ? R20_q : 32'bz;  // Controlled_Buffer controlled_buffer_21
  assign RsData = decoder_2_out21 ? R21_q : 32'bz;  // Controlled_Buffer controlled_buffer_22
  Register #(.width(32)) u_R21 (.D(data_in), .en(and_21_out), .Q(R21_q), .clk(CLK));  // open: clr
  Register #(.width(32)) u_R22 (.D(data_in), .en(and_22_out), .Q(R22_q), .clk(CLK));  // open: clr
  assign RsData = decoder_2_out22 ? R22_q : 32'bz;  // Controlled_Buffer controlled_buffer_23
  Register #(.width(32)) u_R23 (.D(data_in), .en(and_23_out), .Q(R23_q), .clk(CLK));  // open: clr
  assign RsData = decoder_2_out23 ? R23_q : 32'bz;  // Controlled_Buffer controlled_buffer_24
  Register #(.width(32)) u_R24 (.D(data_in), .en(and_24_out), .Q(R24_q), .clk(CLK));  // open: clr
  assign RsData = decoder_2_out24 ? R24_q : 32'bz;  // Controlled_Buffer controlled_buffer_25
  Register #(.width(32)) u_R25 (.D(data_in), .en(and_25_out), .Q(R25_q), .clk(CLK));  // open: clr
  assign RsData = decoder_2_out25 ? R25_q : 32'bz;  // Controlled_Buffer controlled_buffer_26
  assign RsData = decoder_2_out26 ? R26_q : 32'bz;  // Controlled_Buffer controlled_buffer_27
  Register #(.width(32)) u_R26 (.D(data_in), .en(and_26_out), .Q(R26_q), .clk(CLK));  // open: clr
  Register #(.width(32)) u_R27 (.D(data_in), .en(and_27_out), .Q(R27_q), .clk(CLK));  // open: clr
  assign RsData = decoder_2_out27 ? R27_q : 32'bz;  // Controlled_Buffer controlled_buffer_28
  Register #(.width(32)) u_R28 (.D(data_in), .en(and_28_out), .Q(R28_q));  // open: clk, clr
  assign RsData = decoder_2_out28 ? R28_q : 32'bz;  // Controlled_Buffer controlled_buffer_29
  assign RsData = decoder_2_out29 ? R29_q : 32'bz;  // Controlled_Buffer controlled_buffer_30
  Register #(.width(32)) u_R29 (.D(data_in), .en(and_29_out), .Q(R29_q), .clk(CLK));  // open: clr
  assign RsData = decoder_2_out30 ? current_pc : 32'bz;  // Controlled_Buffer controlled_buffer_31
  Register #(.width(32)) u_R30 (.D(data_in), .en(and_30_out), .Q(current_pc), .clk(CLK));  // open: clr
  Register #(.width(32)) u_R31 (.D(data_in), .en(and_31_out), .Q(R31_q), .clk(CLK));  // open: clr
  assign RsData = decoder_2_out31 ? R31_q : 32'bz;  // Controlled_Buffer controlled_buffer_32
  Decoder #(.select(5), .enable("false")) decoder_2 (
    .out0(decoder_2_out0), .out1(decoder_2_out1), .out2(decoder_2_out2), .out3(decoder_2_out3),
    .out4(decoder_2_out4), .out5(decoder_2_out5), .out6(decoder_2_out6), .out7(decoder_2_out7),
    .out8(decoder_2_out8), .out9(decoder_2_out9), .out10(decoder_2_out10), .out11(decoder_2_out11),
    .out12(decoder_2_out12), .out13(decoder_2_out13), .out14(decoder_2_out14), .out15(decoder_2_out15),
    .out16(decoder_2_out16), .out17(decoder_2_out17), .out18(decoder_2_out18), .out19(decoder_2_out19),
    .out20(decoder_2_out20), .out21(decoder_2_out21), .out22(decoder_2_out22), .out23(decoder_2_out23),
    .out24(decoder_2_out24), .out25(decoder_2_out25), .out26(decoder_2_out26), .out27(decoder_2_out27),
    .out28(decoder_2_out28), .out29(decoder_2_out29), .out30(decoder_2_out30), .out31(decoder_2_out31),
    .sel(Rs));
  assign RtData = decoder_3_out0 ? {32{1'b0}} : 32'bz;  // Controlled_Buffer controlled_buffer_33
  assign RtData = decoder_3_out1 ? R1_q : 32'bz;  // Controlled_Buffer controlled_buffer_34
  assign RtData = decoder_3_out2 ? R2_q : 32'bz;  // Controlled_Buffer controlled_buffer_35
  assign RtData = decoder_3_out3 ? R3_q : 32'bz;  // Controlled_Buffer controlled_buffer_36
  assign RtData = decoder_3_out4 ? R4_q : 32'bz;  // Controlled_Buffer controlled_buffer_37
  assign RtData = decoder_3_out5 ? R5_q : 32'bz;  // Controlled_Buffer controlled_buffer_38
  assign RtData = decoder_3_out6 ? R6_q : 32'bz;  // Controlled_Buffer controlled_buffer_39
  assign RtData = decoder_3_out7 ? R7_q : 32'bz;  // Controlled_Buffer controlled_buffer_40
  assign RtData = decoder_3_out8 ? R8_q : 32'bz;  // Controlled_Buffer controlled_buffer_41
  assign RtData = decoder_3_out9 ? R9_q : 32'bz;  // Controlled_Buffer controlled_buffer_42
  assign RtData = decoder_3_out10 ? R10_q : 32'bz;  // Controlled_Buffer controlled_buffer_43
  assign RtData = decoder_3_out11 ? R11_q : 32'bz;  // Controlled_Buffer controlled_buffer_44
  assign RtData = decoder_3_out12 ? R12_q : 32'bz;  // Controlled_Buffer controlled_buffer_45
  assign RtData = decoder_3_out13 ? R13_q : 32'bz;  // Controlled_Buffer controlled_buffer_46
  assign RtData = decoder_3_out14 ? R14_q : 32'bz;  // Controlled_Buffer controlled_buffer_47
  assign RtData = decoder_3_out15 ? R15_q : 32'bz;  // Controlled_Buffer controlled_buffer_48
  assign RtData = decoder_3_out16 ? R16_q : 32'bz;  // Controlled_Buffer controlled_buffer_49
  assign RtData = decoder_3_out17 ? R17_q : 32'bz;  // Controlled_Buffer controlled_buffer_50
  assign RtData = decoder_3_out18 ? R18_q : 32'bz;  // Controlled_Buffer controlled_buffer_51
  assign RtData = decoder_3_out19 ? R19_q : 32'bz;  // Controlled_Buffer controlled_buffer_52
  assign RtData = decoder_3_out20 ? R20_q : 32'bz;  // Controlled_Buffer controlled_buffer_53
  assign RtData = decoder_3_out21 ? R21_q : 32'bz;  // Controlled_Buffer controlled_buffer_54
  assign RtData = decoder_3_out22 ? R22_q : 32'bz;  // Controlled_Buffer controlled_buffer_55
  assign RtData = decoder_3_out23 ? R23_q : 32'bz;  // Controlled_Buffer controlled_buffer_56
  assign RtData = decoder_3_out24 ? R24_q : 32'bz;  // Controlled_Buffer controlled_buffer_57
  assign RtData = decoder_3_out25 ? R25_q : 32'bz;  // Controlled_Buffer controlled_buffer_58
  assign RtData = decoder_3_out26 ? R26_q : 32'bz;  // Controlled_Buffer controlled_buffer_59
  assign RtData = decoder_3_out27 ? R27_q : 32'bz;  // Controlled_Buffer controlled_buffer_60
  assign RtData = decoder_3_out28 ? R28_q : 32'bz;  // Controlled_Buffer controlled_buffer_61
  assign RtData = decoder_3_out29 ? R29_q : 32'bz;  // Controlled_Buffer controlled_buffer_62
  assign RtData = decoder_3_out30 ? current_pc : 32'bz;  // Controlled_Buffer controlled_buffer_63
  assign RtData = decoder_3_out31 ? R31_q : 32'bz;  // Controlled_Buffer controlled_buffer_64
  Decoder #(.select(5), .enable("false")) decoder_3 (
    .out0(decoder_3_out0), .out1(decoder_3_out1), .out2(decoder_3_out2), .out3(decoder_3_out3),
    .out4(decoder_3_out4), .out5(decoder_3_out5), .out6(decoder_3_out6), .out7(decoder_3_out7),
    .out8(decoder_3_out8), .out9(decoder_3_out9), .out10(decoder_3_out10), .out11(decoder_3_out11),
    .out12(decoder_3_out12), .out13(decoder_3_out13), .out14(decoder_3_out14), .out15(decoder_3_out15),
    .out16(decoder_3_out16), .out17(decoder_3_out17), .out18(decoder_3_out18), .out19(decoder_3_out19),
    .out20(decoder_3_out20), .out21(decoder_3_out21), .out22(decoder_3_out22), .out23(decoder_3_out23),
    .out24(decoder_3_out24), .out25(decoder_3_out25), .out26(decoder_3_out26), .out27(decoder_3_out27),
    .out28(decoder_3_out28), .out29(decoder_3_out29), .out30(decoder_3_out30), .out31(decoder_3_out31),
    .sel(Rt));
  assign RpData = decoder_4_out0 ? {32{1'b0}} : 32'bz;  // Controlled_Buffer controlled_buffer_65
  assign RpData = decoder_4_out1 ? R1_q : 32'bz;  // Controlled_Buffer controlled_buffer_66
  assign RpData = decoder_4_out2 ? R2_q : 32'bz;  // Controlled_Buffer controlled_buffer_67
  assign RpData = decoder_4_out3 ? R3_q : 32'bz;  // Controlled_Buffer controlled_buffer_68
  assign RpData = decoder_4_out4 ? R4_q : 32'bz;  // Controlled_Buffer controlled_buffer_69
  assign RpData = decoder_4_out5 ? R5_q : 32'bz;  // Controlled_Buffer controlled_buffer_70
  assign RpData = decoder_4_out6 ? R6_q : 32'bz;  // Controlled_Buffer controlled_buffer_71
  assign RpData = decoder_4_out7 ? R7_q : 32'bz;  // Controlled_Buffer controlled_buffer_72
  assign RpData = decoder_4_out8 ? R8_q : 32'bz;  // Controlled_Buffer controlled_buffer_73
  assign RpData = decoder_4_out9 ? R9_q : 32'bz;  // Controlled_Buffer controlled_buffer_74
  assign RpData = decoder_4_out10 ? R10_q : 32'bz;  // Controlled_Buffer controlled_buffer_75
  assign RpData = decoder_4_out11 ? R11_q : 32'bz;  // Controlled_Buffer controlled_buffer_76
  assign RpData = decoder_4_out12 ? R12_q : 32'bz;  // Controlled_Buffer controlled_buffer_77
  assign RpData = decoder_4_out13 ? R13_q : 32'bz;  // Controlled_Buffer controlled_buffer_78
  assign RpData = decoder_4_out14 ? R14_q : 32'bz;  // Controlled_Buffer controlled_buffer_79
  assign RpData = decoder_4_out15 ? R15_q : 32'bz;  // Controlled_Buffer controlled_buffer_80
  assign RpData = decoder_4_out16 ? R16_q : 32'bz;  // Controlled_Buffer controlled_buffer_81
  assign RpData = decoder_4_out17 ? R17_q : 32'bz;  // Controlled_Buffer controlled_buffer_82
  assign RpData = decoder_4_out18 ? R18_q : 32'bz;  // Controlled_Buffer controlled_buffer_83
  assign RpData = decoder_4_out19 ? R19_q : 32'bz;  // Controlled_Buffer controlled_buffer_84
  assign RpData = decoder_4_out20 ? R20_q : 32'bz;  // Controlled_Buffer controlled_buffer_85
  assign RpData = decoder_4_out21 ? R21_q : 32'bz;  // Controlled_Buffer controlled_buffer_86
  assign RpData = decoder_4_out22 ? R22_q : 32'bz;  // Controlled_Buffer controlled_buffer_87
  assign RpData = decoder_4_out23 ? R23_q : 32'bz;  // Controlled_Buffer controlled_buffer_88
  assign RpData = decoder_4_out24 ? R24_q : 32'bz;  // Controlled_Buffer controlled_buffer_89
  assign RpData = decoder_4_out25 ? R25_q : 32'bz;  // Controlled_Buffer controlled_buffer_90
  assign RpData = decoder_4_out26 ? R26_q : 32'bz;  // Controlled_Buffer controlled_buffer_91
  assign RpData = decoder_4_out27 ? R27_q : 32'bz;  // Controlled_Buffer controlled_buffer_92
  assign RpData = decoder_4_out28 ? R28_q : 32'bz;  // Controlled_Buffer controlled_buffer_93
  assign RpData = decoder_4_out29 ? R29_q : 32'bz;  // Controlled_Buffer controlled_buffer_94
  assign RpData = decoder_4_out30 ? current_pc : 32'bz;  // Controlled_Buffer controlled_buffer_95
  assign RpData = decoder_4_out31 ? R31_q : 32'bz;  // Controlled_Buffer controlled_buffer_96
  Decoder #(.select(5), .enable("false")) decoder_4 (
    .out0(decoder_4_out0), .out1(decoder_4_out1), .out2(decoder_4_out2), .out3(decoder_4_out3),
    .out4(decoder_4_out4), .out5(decoder_4_out5), .out6(decoder_4_out6), .out7(decoder_4_out7),
    .out8(decoder_4_out8), .out9(decoder_4_out9), .out10(decoder_4_out10), .out11(decoder_4_out11),
    .out12(decoder_4_out12), .out13(decoder_4_out13), .out14(decoder_4_out14), .out15(decoder_4_out15),
    .out16(decoder_4_out16), .out17(decoder_4_out17), .out18(decoder_4_out18), .out19(decoder_4_out19),
    .out20(decoder_4_out20), .out21(decoder_4_out21), .out22(decoder_4_out22), .out23(decoder_4_out23),
    .out24(decoder_4_out24), .out25(decoder_4_out25), .out26(decoder_4_out26), .out27(decoder_4_out27),
    .out28(decoder_4_out28), .out29(decoder_4_out29), .out30(decoder_4_out30), .out31(decoder_4_out31),
    .sel(Rp));

  assign next_pc = data_in;
  // also tied to GND on the sheet: decoder_1_out0
endmodule

module ALU (
  input  [31:0] IN1,
  input  [31:0] IN2,
  input  [2:0] AluSel,
  output [31:0] ALUres
);

  wire [31:0] adder_1_out, and_1_out, nor_1_out, or_1_out, subtractor_1_out;

  Adder #(.width(32)) adder_1 (.a(IN1), .b(IN2), .out(adder_1_out), .cin(1'b0));  // open: cout
  Subtractor #(.width(32)) subtractor_1 (.a(IN1), .b(IN2), .out(subtractor_1_out), .bin(1'b0));  // open: bout
  assign or_1_out = IN1 | IN2;  // OR_Gate or_1, 32 bits wide
  assign nor_1_out = ~(IN1 | IN2);  // NOR_Gate nor_1, 32 bits wide
  assign and_1_out = IN1 & IN2;  // AND_Gate and_1, 32 bits wide
  Multiplexer #(.select(3), .width(32), .disabled(0), .enable("false")) multiplexer_1 (
    .in0(adder_1_out), .in1(subtractor_1_out), .in2(or_1_out), .in3(nor_1_out), .in4(and_1_out),
    .in5({32{1'b0}}), .in6({32{1'b0}}), .in7({32{1'b0}}), .out(ALUres), .sel(AluSel));
endmodule

module Extender (
  input  [11:0] Imm12,
  input  [21:0] Offset22,
  input  [1:0] ExtSel,
  output [31:0] ExOut
);

  wire [31:0] bit_extender_1_out, bit_extender_2_out, bit_extender_3_out;

  assign bit_extender_1_out = {{20{1'b0}}, Imm12};  // Bit_Extender bit_extender_1
  assign bit_extender_2_out = {{20{Imm12[11]}}, Imm12};  // Bit_Extender bit_extender_2
  assign bit_extender_3_out = {{10{Offset22[21]}}, Offset22};  // Bit_Extender bit_extender_3
  Multiplexer #(.select(2), .width(32), .enable("false")) multiplexer_1 (
    .in0(bit_extender_1_out), .in1(bit_extender_2_out), .in2(bit_extender_3_out), .in3({32{1'b0}}),
    .out(ExOut), .sel(ExtSel));
endmodule

module PredicateUnit (
  input  [31:0] Rp_data,
  input  [4:0] Rp_addr,
  output ExecuteEn
);

  wire comparator_1_eq, comparator_2_eq, not_1_out;

  Comparator #(.width(32)) comparator_1 (.a({32{1'b0}}), .b(Rp_data), .eq(comparator_1_eq));  // open: gt, lt
  Comparator #(.width(5)) comparator_2 (.a(Rp_addr), .b({5{1'b0}}), .eq(comparator_2_eq));  // open: gt, lt
  not not_1 (not_1_out, comparator_1_eq);
  or or_1 (ExecuteEn, not_1_out, comparator_2_eq);
endmodule

module PC_Control (
  input  [31:0] current_pc,
  input  [31:0] sign_ext_off,
  input  [31:0] rs_data,
  input  ExecuteEn,
  input  [1:0] PCSrc,
  output [31:0] next_pc
);

  wire [31:0] adder_1_out, multiplexer_1_out, multiplexer_2_out, PC_1;

  Adder #(.width(32)) adder_1 (.a(current_pc), .b(sign_ext_off), .out(adder_1_out), .cin(1'b0));  // open: cout
  Multiplexer #(.width(32), .enable("false")) multiplexer_1 (
    .in0(PC_1), .in1(adder_1_out), .out(multiplexer_1_out), .sel(ExecuteEn));
  Multiplexer #(.width(32), .enable("false")) multiplexer_2 (
    .in0(PC_1), .in1(rs_data), .out(multiplexer_2_out), .sel(ExecuteEn));
  Adder #(.width(32)) adder_2 (.a(current_pc), .b(32'h1), .out(PC_1), .cin(1'b0));  // open: cout
  Multiplexer #(.select(2), .width(32), .enable("false")) multiplexer_3 (
    .in0(PC_1), .in1(multiplexer_1_out), .in2(multiplexer_2_out), .in3(PC_1), .out(next_pc), .sel(PCSrc));
endmodule

module ControlUnit (
  input  [4:0] Opcode,
  output RegWrite,
  output ALUSrc,
  output RegDst,
  output MemRead,
  output MemWrite,
  output RegReadSrc2,
  output [1:0] WB_Sel,
  output [2:0] ALUOp,
  output [1:0] PCSel,
  output [1:0] ExtSel
);

  ROM #(.addrWidth(5), .dataWidth(15)) rom_1 (
    .addr(Opcode),
    .data({ExtSel, PCSel, ALUOp, WB_Sel, RegReadSrc2, MemWrite, MemRead, RegDst, ALUSrc, RegWrite}));  // open: sel

  // Notes on the sheet:
  //   contents of rom_1 (hex, n*v repeats v):
  //   1 201 401 601 801 4005 405 605 809 4095 4046 5*0 1000 1109 2000 5*588 8*598
endmodule

module IF_ID (
  input  [31:0] Instruction_F,
  input  [31:0] PC_F,
  input  stall,
  input  clk,
  input  kill,
  output [31:0] Instruction_D,
  output [31:0] PC_D
);

  wire not_1_out;

  not not_1 (not_1_out, stall);
  Register #(.width(32)) Instrruction_Reg (.D(Instruction_F), .en(not_1_out), .Q(Instruction_D), .clk(clk), .clr(kill));
  Register #(.width(32)) PC_Reg (.D(PC_F), .en(not_1_out), .Q(PC_D), .clk(clk), .clr(kill));
endmodule

module ID_EX (
  input  RegWrite_D,
  input  MemRead_D,
  input  MemWrite_D,
  input  ALUSrc_D,
  input  [1:0] WB_Sel_D,
  input  [2:0] ALU_OP_D,
  input  [31:0] RsData_D,
  input  [31:0] RtData_D,
  input  [31:0] ExtImm_D,
  input  [31:0] PC_plus_1_D,
  input  [4:0] Rd_Addr_D,
  input  [4:0] Rs_Addr_D,
  input  [4:0] Rt_Addr_D,
  input  CLK,
  input  stall,
  input  kill,
  output RegWrite_EX,
  output MemRead_EX,
  output MemWrite_EX,
  output ALUSrc_EX,
  output [1:0] WB_Sel_EX,
  output [2:0] ALU_OP_EX,
  output [31:0] RsData_EX,
  output [31:0] RtData_EX,
  output [31:0] ExtImm_EX,
  output [31:0] PC_plus_1_EX,
  output [4:0] Rd_Addr_EX,
  output [4:0] Rs_Addr_EX,
  output [4:0] Rt_Addr_EX
);

  wire or_1_out;

  Register #(.width(1)) RegWrite (.D(RegWrite_D), .Q(RegWrite_EX), .clk(CLK), .clr(or_1_out));  // open: en
  Register #(.width(1)) MemRead (.D(MemRead_D), .Q(MemRead_EX), .clk(CLK), .clr(or_1_out));  // open: en
  Register #(.width(1)) MemWrite (.D(MemWrite_D), .Q(MemWrite_EX), .clk(CLK), .clr(or_1_out));  // open: en
  Register #(.width(1)) ALUSrc (.D(ALUSrc_D), .Q(ALUSrc_EX), .clk(CLK), .clr(or_1_out));  // open: en
  Register #(.width(2)) WB_Sel (.D(WB_Sel_D), .Q(WB_Sel_EX), .clk(CLK), .clr(or_1_out));  // open: en
  Register #(.width(3)) ALU_OP (.D(ALU_OP_D), .Q(ALU_OP_EX), .clk(CLK), .clr(or_1_out));  // open: en
  Register #(.width(32)) RsData (.D(RsData_D), .Q(RsData_EX), .clk(CLK), .clr(or_1_out));  // open: en
  Register #(.width(32)) RtData (.D(RtData_D), .Q(RtData_EX), .clk(CLK), .clr(or_1_out));  // open: en
  Register #(.width(32)) RtData_2 (.D(ExtImm_D), .Q(ExtImm_EX), .clk(CLK), .clr(or_1_out));  // open: en
  Register #(.width(32)) PC_plus_1 (.D(PC_plus_1_D), .Q(PC_plus_1_EX), .clk(CLK), .clr(or_1_out));  // open: en
  Register #(.width(5)) Rd_Addr (.D(Rd_Addr_D), .Q(Rd_Addr_EX), .clk(CLK), .clr(or_1_out));  // open: en
  Register #(.width(5)) Rs_Addr (.D(Rs_Addr_D), .Q(Rs_Addr_EX), .clk(CLK), .clr(or_1_out));  // open: en
  Register #(.width(5)) Rt_Addr (.D(Rt_Addr_D), .Q(Rt_Addr_EX), .clk(CLK), .clr(or_1_out));  // open: en
  or or_1 (or_1_out, stall, kill);
endmodule

module EX_MEM (
  input  RegWrite_EX,
  input  MemRead_EX,
  input  MemWrite_EX,
  input  [1:0] WB_Sel_EX,
  input  [31:0] ALU_Result_EX,
  input  [31:0] WriteData_EX,
  input  [31:0] PC_plus_1_EX,
  input  [4:0] Rd_Addr_EX,
  input  clk,
  output RegWrite_MEM,
  output MemRead_MEM,
  output MemWrite_MEM,
  output [1:0] WB_Sel_MEM,
  output [31:0] ALU_Result_MEM,
  output [31:0] WriteData_MEM,
  output [31:0] PC_plus_1_MEM,
  output [4:0] Rd_Addr_MEM
);

  Register #(.width(1)) RegWrite (.D(RegWrite_EX), .Q(RegWrite_MEM), .clk(clk));  // open: en, clr
  Register #(.width(1)) MemReaad (.D(MemRead_EX), .Q(MemRead_MEM), .clk(clk));  // open: en, clr
  Register #(.width(1)) MemWrite (.D(MemWrite_EX), .Q(MemWrite_MEM), .clk(clk));  // open: en, clr
  Register #(.width(2)) WB_Sel (.D(WB_Sel_EX), .Q(WB_Sel_MEM), .clk(clk));  // open: en, clr
  Register #(.width(32)) ALU_Result (.D(ALU_Result_EX), .Q(ALU_Result_MEM), .clk(clk));  // open: en, clr
  Register #(.width(32)) WriteData (.D(WriteData_EX), .Q(WriteData_MEM), .clk(clk));  // open: en, clr
  Register #(.width(32)) PC_plus_1 (.D(PC_plus_1_EX), .Q(PC_plus_1_MEM), .clk(clk));  // open: en, clr
  Register #(.width(5)) Rd_Addr (.D(Rd_Addr_EX), .Q(Rd_Addr_MEM), .clk(clk));  // open: en, clr
endmodule

module MEM_WB (
  input  RegWrite_MEM,
  input  [1:0] WB_Sel_MEM,
  input  [31:0] ALU_Result_MEM,
  input  [31:0] MemData_MEM,
  input  [31:0] PC_plus_1_MEM,
  input  [4:0] Rd_Addr_MEM,
  input  clk,
  output RegWrite_WB,
  output [1:0] WB_Sel_WB,
  output [31:0] ALU_Result_WB,
  output [31:0] MemData_WB,
  output [31:0] PC_plus_1_WB,
  output [4:0] Rd_Addr_WB
);

  Register #(.width(1)) RegWrite (.D(RegWrite_MEM), .Q(RegWrite_WB), .clk(clk), .clr(clk));  // open: en
  Register #(.width(2)) WB_Sel (.D(WB_Sel_MEM), .Q(WB_Sel_WB), .clk(clk));  // open: en, clr
  Register #(.width(32)) ALU_Result (.D(ALU_Result_MEM), .Q(ALU_Result_WB), .clk(clk));  // open: en, clr
  Register #(.width(32)) MemData (.D(MemData_MEM), .Q(MemData_WB), .clk(clk));  // open: en, clr
  Register #(.width(32)) PC_plus_1 (.D(PC_plus_1_MEM), .Q(PC_plus_1_WB), .clk(clk));  // open: en, clr
  Register #(.width(5)) Rd_Addr (.D(Rd_Addr_MEM), .Q(Rd_Addr_WB), .clk(clk));  // open: en, clr
endmodule

module ForwardingUnit (
  input  [4:0] SrcAddr,
  input  [4:0] Rd_Ex,
  input  RegWrite_EX,
  input  [4:0] Rd_MEM,
  input  RegWrite_MEM,
  input  [4:0] Rd_WB,
  input  RegWrite_WB,
  output [1:0] Forward
);

  wire and_1_out, and_2_out, and_3_out, and_4_out, and_5_out, comparator_1_eq, comparator_2_eq,
       comparator_3_eq, comparator_4_eq, not_2_out, not_3_out, R0_Check;

  Comparator #(.width(5)) comparator_1 (.a(SrcAddr), .b(Rd_Ex), .eq(comparator_1_eq));  // open: gt, lt
  Comparator #(.width(5)) comparator_2 (.a(SrcAddr), .b(Rd_MEM), .eq(comparator_2_eq));  // open: gt, lt
  Comparator #(.width(5)) comparator_3 (.a(SrcAddr), .b(Rd_WB), .eq(comparator_3_eq));  // open: gt, lt
  Comparator #(.width(5)) comparator_4 (.a(SrcAddr), .b({5{1'b0}}), .eq(comparator_4_eq));  // open: gt, lt
  and and_1 (and_1_out, comparator_1_eq, RegWrite_EX, R0_Check);
  not not_1 (R0_Check, comparator_4_eq);
  and and_2 (and_2_out, comparator_2_eq, RegWrite_MEM, R0_Check);
  and and_3 (and_3_out, comparator_3_eq, RegWrite_WB, R0_Check);
  not not_2 (not_2_out, and_1_out);
  not not_3 (not_3_out, and_2_out);
  and and_4 (and_4_out, and_2_out, not_2_out);
  and and_5 (and_5_out, and_3_out, not_2_out, not_3_out);
  or or_1 (Forward[0], and_1_out, and_5_out);
  or or_2 (Forward[1], and_4_out, and_5_out);
endmodule

module KillUnit (
  input  [4:0] Opcode,
  input  ExecuteEn,
  output Kill
);

  wire comparator_1_eq, comparator_2_eq, comparator_3_eq, or_1_out;

  Comparator #(.width(5)) comparator_1 (.a(Opcode), .b(5'b01011), .eq(comparator_1_eq));  // open: gt, lt
  Comparator #(.width(5)) comparator_2 (.a(Opcode), .b(5'b01100), .eq(comparator_2_eq));  // open: gt, lt
  Comparator #(.width(5)) comparator_3 (.a(Opcode), .b(5'b01101), .eq(comparator_3_eq));  // open: gt, lt
  or or_1 (or_1_out, comparator_1_eq, comparator_2_eq, comparator_3_eq);
  and and_1 (Kill, ExecuteEn, or_1_out);
endmodule

module StallUnit (
  input  [1:0] forrward_rs,
  input  MemRead_EX,
  input  [1:0] forward_rt,
  input  [1:0] forward_rp,
  output Stall
);

  wire comparator_1_eq, comparator_2_eq, comparator_3_eq, or_1_out;

  Comparator #(.width(2)) comparator_1 (.a(2'b01), .b(forrward_rs), .eq(comparator_1_eq));  // open: gt, lt
  Comparator #(.width(2)) comparator_2 (.a(2'b01), .b(forward_rt), .eq(comparator_2_eq));  // open: gt, lt
  Comparator #(.width(2)) comparator_3 (.a(2'b01), .b(forward_rp), .eq(comparator_3_eq));  // open: gt, lt
  or or_1 (or_1_out, comparator_1_eq, comparator_2_eq, comparator_3_eq);
  and and_1 (Stall, MemRead_EX, or_1_out);
endmodule

module DecodeStage_splitter (
  input  [31:0] Inst,
  output [4:0] OPCode,
  output [4:0] Rp,
  output [4:0] Rd,
  output [4:0] Rs,
  output [4:0] Rt,
  output [11:0] Immediate,
  output [21:0] Offset
);


  assign Immediate = Inst[11:0];
  assign Offset = Inst[21:0];
  assign OPCode = Inst[31:27];
  assign Rd = Inst[21:17];
  assign Rp = Inst[26:22];
  assign Rs = Inst[16:12];
  assign Rt = Inst[11:7];

  // Other names for the same wires on the sheet: Unused[6:0] = Inst[6:0]
endmodule
